# Fritzing sketch Connection ESP32 - Arduino ONE (saved by Fritzing 0.9.3b)

parts:
  Part1 = Arduino Uno (Rev3)
  U1 = ESP 32 DEVKIT DOIT

nets:
  N1: Part1.D0/RX, U1.RX0
  N2: Part1.D1/TX, U1.TX0
  3V3: Part1.3V3, U1.D22, U1.3V3
  GND: Part1.GND, U1.GND

// code stored in the sketch: ESP32 - Arduino ONE.ino
#include <WiFi.h>
#include <PubSubClient.h>

#define WIFISSID "---" 
#define PASSWORD "---" 
#define TOKEN "---" 
#define MQTT_CLIENT_NAME "1234a5d6798" 



#define VARIABLE_LABEL "sensor" 
#define DEVICE_LABEL "esp32" 

#define SENSOR A0 

char mqttBroker[]  = "industrial.api.ubidots.com";
char payload[100];
char topic[150];
// Space to store values to send
char str_sensor[10];


WiFiClient ubidots;
PubSubClient client(ubidots);

void callback(char* topic, byte* payload, unsigned int length) {
  char p[length + 1];
  memcpy(p, payload, length);
  p[length] = NULL;
  Serial.write(payload, length);
  Serial.println(topic);
}

void reconnect() {

  while (!client.connected()) {
    Serial.println("Attempting MQTT connection...");
    

    if (client.connect(MQTT_CLIENT_NAME, TOKEN, "")) {
      Serial.println("Connected");
    } else {
      Serial.print("Failed, rc=");
      Serial.print(client.state());
      Serial.println(" try again in 2 seconds");

      delay(2000);
    }
  }
}


void setup() {
  Serial.begin(115200);
  WiFi.begin(WIFISSID, PASSWORD);

  pinMode(SENSOR, INPUT);

  Serial.println();
  Serial.print("Waiting for WiFi...");
  
  while (WiFi.status() != WL_CONNECTED) {
    Serial.print(".");
    delay(500);
  }
  
  Serial.println("");
  Serial.println("WiFi Connected");
  Serial.println("IP address: ");
  Serial.println(WiFi.localIP());
  client.setServer(mqttBroker, 1883);
  client.setCallback(callback);  
}

void loop() {
  if (!client.connected()) {
    reconnect();
  }

  sprintf(topic, "%s%s", "/v1.6/devices/", DEVICE_LABEL);
  sprintf(payload, "%s", ""); 
  sprintf(payload, "{\"%s\":", VARIABLE_LABEL); 
  
  float sensor = analogRead(SENSOR); 
  

  dtostrf(sensor, 4, 2, str_sensor);
  
  sprintf(payload, "%s {\"value\": %s}}", payload, str_sensor); 
  Serial.println("Publishing data to Ubidots Cloud");
  client.publish(topic, payload);
  client.loop();
  delay(500);
}
